# Fritzing sketch calcUABlator-fritzing (saved by Fritzing 1.0.1rc)
breadboards: 1

parts:
  M1 = Stepper Motor - Bipolar
  M2 = Stepper Motor - Bipolar
  Pololu_A1 = Pololu A4988 [package=SO16]
  Pololu_A2 = Pololu A4988 [package=SO16]
  Componente1 = Arduino Uno (Rev3)
  J1 = Basic Servo
  VCC1 = Battery block 9V
  Raspberry_Pi_1 = Raspberry Pi 3 [part_number=RPI-3-V1.2]  # not connected

nets:
  N1: M1.A, Pololu_A1.2B
  N2: M1.C, Pololu_A1.2A
  N3: M1.B, Pololu_A1.1A
  N4: M1.D, Pololu_A1.1B
  N5: M2.A, Pololu_A2.2B
  N6: M2.C, Pololu_A2.2A
  N7: M2.B, Pololu_A2.1A
  N8: M2.D, Pololu_A2.1B
  GND: Pololu_A1.GND, Pololu_A2.GND, Componente1.GND, J1.gnd, VCC1.-
  VDD: Pololu_A1.VDD, Pololu_A2.VDD, Componente1.5V, J1.vcc
  N9: Pololu_A1.VMOT, Pololu_A2.VMOT, VCC1.+
  N10: Componente1.D9_PWM, J1.pulse
